# Fritzing sketch LEDMatrix (saved by Fritzing 0.8.7b)
breadboards: 1

parts:
  Onderdeel1 = Logic Level Converter
  NEOPIXEL1 = Neopixel 8x8 Matrix
  Onderdeel2 = Arduino Uno (Rev3)
  U1 = mystery part, 3 pins [chip_label=Pineapple]  # not connected
  U1_2 = mystery part, 4 pins [chip_label=Pineapple]
  J1 = Power Jack [package=power_jack_pth_lock]
  C1 = Electrolytic Capacitor [capacitance=1000μF package="1010 [SMD, electrolytic]"]
  R1 = Resistor [tolerance=±2% resistance=330 package="0603 [SMD]"]

nets:
  N1: Onderdeel1.TX2_LV, U1_2.pin2
  N2: Onderdeel1.RX2_LV, U1_2.pin3
  GND: Onderdeel1.GND, NEOPIXEL1.GND, Onderdeel2.GND, U1_2.pin4, J1.GND, C1.-
  N3: Onderdeel1.LV, Onderdeel2.3V3
  N4: Onderdeel1.HV, Onderdeel2.5V
  N5: Onderdeel1.RX2_HV, Onderdeel2.D1/TX
  N6: Onderdeel1.TX2_HV, Onderdeel2.D0/RX
  N7: NEOPIXEL1.DIN, R1.Pin_1
  N8: NEOPIXEL1.VCC, J1.PWR, C1.+
  N9: Onderdeel2.D6_PWM, R1.Pin_0

notes:
  Pineapple MKV

custom parts:
  Neopixel 8x8 Matrix: Adafruit Neopixel 8x8 Matrix
